# Fritzing sketch control_circuit (saved by Fritzing 0.9.3b)
breadboards: 1

parts:
  photocell = Arduino Uno (Rev3)
  LED = LED - 5mm [color="Red (635nm)" package="5 mm [THT]"]
  R2 = Resistor [tolerance=±5% resistance=4.7k package=THT]
  R1 = Resistor [tolerance=±5% resistance=330 package=THT]
  R3 = Photocell (LDR) [package=THT]

nets:
  N1: photocell.A0, R2.Pin_1, R3.pin_1
  N2: photocell.D5_PWM, R1.Pin_1
  N3: photocell.5V, R3.pin_0
  N4: photocell.GND, LED.cathode, R2.Pin_0
  N5: LED.anode, R1.Pin_0
